// Logisim project 3-bit Parity Checker.circ as structural Verilog: 1 circuit, main circuit main
module main (
  input  in_1,
  input  in_2,
  input  in_3,
  input  P,
  input  in_5,
  input  in_6,
  input  in_7,
  input  P_2,
  output Even,
  output Odd
);

  wire xnor_1_out, xnor_2_out, xor_1_out, xor_2_out;

  xor xor_1 (xor_1_out, in_1, in_2);
  xor xor_2 (xor_2_out, in_3, P);
  xnor xnor_1 (xnor_1_out, in_5, in_6);
  xnor xnor_2 (xnor_2_out, in_7, P_2);
  xor xor_3 (Even, xor_1_out, xor_2_out);
  xnor xnor_3 (Odd, xnor_1_out, xnor_2_out);
endmodule
