// Logisim project 3-bit Parity Generator.circ as structural Verilog: 1 circuit, main circuit main
module main (
  input  in_1,
  input  in_2,
  input  in_3,
  input  in_4,
  input  in_5,
  input  in_6,
  output Even,
  output Odd
);

  wire not_1_out, xor_1_out, xor_2_out;

  xor xor_1 (xor_1_out, in_1, in_2);
  xor xor_2 (xor_2_out, in_4, in_5);
  not not_1 (not_1_out, in_6);
  xor xor_3 (Even, xor_1_out, in_3);
  xor xor_4 (Odd, xor_2_out, not_1_out);
endmodule
