// Logisim project JK Flip-Flop.circ as structural Verilog: 1 circuit, main circuit main
module main (
  input  in_1,
  input  in_2,
  output out_3,
  output out_4,
  output out_5,
  output out_6
);

  wire clock_1_out, nand_1_out, nand_2_out, nand_4_out, nand_5_out, nand_6_out, nand_8_out, nand_9_out,
       nand_10_out, nand_12_out, nand_13_out, nand_14_out, nand_16_out;

  Clock clock_1 (.out(clock_1_out));
  nand nand_1 (nand_1_out, in_1, nand_4_out, clock_1_out);
  nand nand_2 (nand_2_out, clock_1_out, out_3, in_2);
  nand nand_3 (out_3, nand_1_out, nand_4_out);
  nand nand_4 (nand_4_out, out_3, nand_2_out);
  nand nand_5 (nand_5_out, out_3, nand_8_out, clock_1_out);
  nand nand_6 (nand_6_out, clock_1_out, out_4, nand_4_out);
  nand nand_7 (out_4, nand_5_out, nand_8_out);
  nand nand_8 (nand_8_out, out_4, nand_6_out);
  nand nand_9 (nand_9_out, out_4, nand_12_out, clock_1_out);
  nand nand_10 (nand_10_out, clock_1_out, out_5, nand_8_out);
  nand nand_11 (out_5, nand_9_out, nand_12_out);
  nand nand_12 (nand_12_out, out_5, nand_10_out);
  nand nand_13 (nand_13_out, out_5, nand_16_out, clock_1_out);
  nand nand_14 (nand_14_out, clock_1_out, out_6, nand_12_out);
  nand nand_15 (out_6, nand_13_out, nand_16_out);
  nand nand_16 (nand_16_out, out_6, nand_14_out);
endmodule
