// Logisim project Full Adder & Subtractor.circ as structural Verilog: 1 circuit, main circuit main
module main (
  input  in_1,
  input  in_2,
  input  in_3,
  output Sum,
  output Carry,
  output Difference,
  output Borrow
);

  wire and_1_out, and_2_out, and_3_out, and_4_out, buffer_1_out, buffer_2_out, xor_1_out, xor_2_out;

  buf buffer_1 (buffer_1_out, in_1);
  xor xor_1 (xor_1_out, in_1, in_2);
  and and_1 (and_1_out, in_1, in_2);
  xor xor_2 (xor_2_out, in_1, in_2);
  and and_2 (and_2_out, buffer_1_out, in_2);
  buf buffer_2 (buffer_2_out, xor_2_out);
  xor xor_3 (Sum, xor_1_out, in_3);
  and and_3 (and_3_out, xor_1_out, in_3);
  xor xor_4 (Difference, xor_2_out, in_3);
  and and_4 (and_4_out, buffer_2_out, in_3);
  or or_1 (Carry, and_3_out, and_1_out);
  or or_2 (Borrow, and_4_out, and_2_out);
endmodule
