// Logisim project Half Adder & Subtractor.circ as structural Verilog: 1 circuit, main circuit main
module main (
  input  in_1,
  input  in_2,
  output Sum,
  output Carry,
  output Difference,
  output Borrow
);

  wire buffer_1_out;

  buf buffer_1 (buffer_1_out, in_1);
  xor xor_1 (Sum, in_1, in_2);
  and and_1 (Carry, in_1, in_2);
  xor xor_2 (Difference, in_1, in_2);
  and and_2 (Borrow, buffer_1_out, in_2);
endmodule
