// Logisim project SR_flipflop.circ as structural Verilog: 1 circuit, main circuit main
module main (
  input  S,
  input  R,
  output Q,
  output R_2
);

  wire clock_1_out, nand_1_out, nand_2_out;

  Clock clock_1 (.out(clock_1_out));
  nand nand_1 (nand_1_out, S, clock_1_out);
  nand nand_2 (nand_2_out, clock_1_out, R);
  nand nand_3 (Q, nand_1_out, R_2);
  nand nand_4 (R_2, Q, nand_2_out);
endmodule
